# Fritzing sketch AirWick_Wifi (saved by Fritzing 0.9.5d)

parts:
  WeMos_D1_Mini1 = WeMos D1 Mini
  M2 = DC Motor
  R1 = PHOTOCELL [package=photocell]
  R2 = Resistor [tolerance=±5% resistance=10k package=THT]  # not connected
  R3 = Resistor [tolerance=±5% resistance=10k package=THT]
  R4 = Resistor [tolerance=±5% resistance=100 package=THT]
  IRF3250 = Basic FET N-Channel [package="DPak [SMD]"]
  M3 = TP4056 Module [part_number=HW-107]
  U1 = LIPO-1000mAh [package=lipo-1000]
  S1 = Square Pushbutton
  U2 = SWITCH_SPDT [package=kps-1290]

nets:
  N1: WeMos_D1_Mini1.5V, U2.S
  N2: WeMos_D1_Mini1.A0, R1.P$1, R3.Pin_0
  N3: WeMos_D1_Mini1.D0, WeMos_D1_Mini1.RST
  N4: WeMos_D1_Mini1.D1, R4.Pin_0
  N5: WeMos_D1_Mini1.D3, S1.leg1
  N6: WeMos_D1_Mini1.G, M3.OUT-#1
  N7: M2.pin_2, IRF3250.drain
  N8: R4.Pin_1, IRF3250.Gate
  N9: M3.BAT-, U1.-
  N10: M3.BAT+, U1.+
  N11: M3.OUT-#4, U2.P

custom parts:
  TP4056 Module: TP4056 Lithium Battery Charge Management Module Links: TP4056 website
